// Logisim project CPU.circ as structural Verilog: 5 circuits, main circuit main
module main (
  input  Clear
);

  wire clock_1_out, control_1__2, control_1__3, control_1__4, control_1__5, control_1__6, control_1__7,
       control_1__8, control_1_ldhi, n16_bit_alu_1_zero;
  wire [1:0] control_1__1_2;
  wire [3:0] control_1__1;
  wire [15:0] alu_adder_1_out_3, alu_adder_2_out_3, bit_extender_1_out, bit_extender_2_out,
       multiplexer_1_out, multiplexer_2_out, multiplexer_3_out, multiplexer_4_out, multiplexer_5_out,
       multiplexer_6_out, multiplexer_7_out, multiplexer_8_out, multiplexer_9_out, n16_bit_alu_1_out_5,
       ram_1_data, ram_2_data, register_1_q, register_file_1_out_7, register_file_1_out_8,
       register_file_1_out_9, shifter_1_out;

  ALU_adder alu_adder_1 (.in_1(register_1_q), .in_2(multiplexer_1_out), .out_3(alu_adder_1_out_3));
  Clock clock_1 (.out(clock_1_out));
  Register #(.width(16), .trigger("falling")) register_1 (
    .D(alu_adder_1_out_3), .Q(register_1_q), .clk(clock_1_out), .clr(Clear));  // open: en
  Multiplexer #(.width(16), .enable("false")) multiplexer_1 (
    .in0(multiplexer_2_out), .in1(bit_extender_2_out), .out(multiplexer_1_out), .sel(control_1__8));
  ALU_adder alu_adder_2 (.in_1(register_1_q), .in_2(16'h1), .out_3(alu_adder_2_out_3));
  Multiplexer #(.select(2), .width(16), .enable("false")) multiplexer_2 (
    .in0(16'h1), .in1(multiplexer_3_out), .in2(multiplexer_4_out), .in3(bit_extender_1_out),
    .out(multiplexer_2_out), .sel(control_1__1_2));
  RAM #(.addrWidth(16), .dataWidth(16)) ram_1 (
    .addr(register_1_q), .data(ram_1_data), .clk(clock_1_out), .clr(Clear));  // open: sel, ld
  Multiplexer #(.width(16), .enable("false")) multiplexer_3 (
    .in0(bit_extender_2_out), .in1(16'h1), .out(multiplexer_3_out), .sel(n16_bit_alu_1_zero));
  Multiplexer #(.width(16), .enable("false")) multiplexer_4 (
    .in0(16'h1), .in1(bit_extender_2_out), .out(multiplexer_4_out), .sel(n16_bit_alu_1_zero));
  assign bit_extender_1_out = {{4{1'b0}}, ram_1_data[11:0]};  // Bit_Extender bit_extender_1
  Control control_1 (
    .in_1(ram_1_data[15:12]), ._4(control_1__4), ._6(control_1__6), ._7(control_1__7), ._8(control_1__8),
    ._5(control_1__5), ._1(control_1__1), ._1_2(control_1__1_2), ._3(control_1__3), ._2(control_1__2),
    .ldhi(control_1_ldhi));
  assign bit_extender_2_out = {{8{ram_1_data[7]}}, ram_1_data[7:0]};  // Bit_Extender bit_extender_2
  Register_file register_file_1 (
    .in_2(ram_1_data[3:0]), .out_7(register_file_1_out_7), .out_8(register_file_1_out_8),
    .Write(control_1__2), .in_5(clock_1_out), .in_1(multiplexer_5_out), .out_9(register_file_1_out_9),
    .Register_number(ram_1_data[7:4]), .Read_register_2(ram_1_data[11:8]));
  Multiplexer #(.width(16), .enable("false")) multiplexer_5 (
    .in0(multiplexer_8_out), .in1(shifter_1_out), .out(multiplexer_5_out), .sel(control_1_ldhi));
  Multiplexer #(.width(16), .enable("false")) multiplexer_6 (
    .in0(register_file_1_out_7), .in1(register_file_1_out_9), .out(multiplexer_6_out), .sel(control_1__7));
  Multiplexer #(.width(16), .enable("false")) multiplexer_7 (
    .in0(register_file_1_out_8), .in1(bit_extender_2_out), .out(multiplexer_7_out), .sel(control_1__3));
  Shifter #(.width(16)) shifter_1 (.in(bit_extender_2_out), .\dist (4'b1000), .out(shifter_1_out));
  Multiplexer #(.width(16), .enable("false")) multiplexer_8 (
    .in0(multiplexer_9_out), .in1(alu_adder_2_out_3), .out(multiplexer_8_out), .sel(control_1__8));
  _16_bit_ALU u_16_bit_alu_1 (
    .in_2(multiplexer_6_out), .in_3(multiplexer_7_out), .zero(n16_bit_alu_1_zero),
    .out_5(n16_bit_alu_1_out_5), .OP(control_1__1));
  Multiplexer #(.width(16), .enable("false")) multiplexer_9 (
    .in0(ram_2_data), .in1(n16_bit_alu_1_out_5), .out(multiplexer_9_out), .sel(control_1__6));
  RAM #(.addrWidth(16), .dataWidth(16), .bus("separate")) ram_2 (
    .addr(n16_bit_alu_1_out_5), .din(register_file_1_out_9), .data(ram_2_data), .str(control_1__5),
    .clk(clock_1_out), .ld(control_1__4), .clr(Clear));  // open: sel

  // Notes on the sheet:
  //   Clock
  //   Xiomara Figueroa Fontánez
  //   Computer Architecture
  //   CCOM4086
  //   prof. Humberto Ortíz
  //   Jal
  //   PC  src
  //   B NZ
  //   B Z
  //   jump
  //   Write RD?
  //   RS 0 RD
  //   ALUsrc
  //   ldhi
  //   ALU  control
  //   memReg
  //   mem  Write
  //   mem  Read
  //   Nótese el esfuerzo por que se vea lindo.
endmodule

module Register_file (
  input  [15:0] in_1,
  input  [3:0] in_2,
  input  [3:0] Register_number,
  input  [3:0] Read_register_2,
  input  in_5,
  input  Write,
  output [15:0] out_7,
  output [15:0] out_8,
  output [15:0] out_9
);

  wire and_1_out, and_2_out, and_3_out, and_4_out, and_5_out, and_6_out, and_7_out, and_8_out, and_9_out,
       and_10_out, and_11_out, and_12_out, and_13_out, and_14_out, and_15_out, and_16_out, decoder_1_out0,
       decoder_1_out1, decoder_1_out2, decoder_1_out3, decoder_1_out4, decoder_1_out5, decoder_1_out6,
       decoder_1_out7, decoder_1_out8, decoder_1_out9, decoder_1_out10, decoder_1_out11, decoder_1_out12,
       decoder_1_out13, decoder_1_out14, decoder_1_out15;
  wire [15:0] register_1_q, register_2_q, register_3_q, register_4_q, register_5_q, register_6_q,
       register_7_q, register_8_q, register_9_q, register_10_q, register_11_q, register_12_q, register_13_q,
       register_14_q, register_15_q, register_16_q;

  Decoder #(.select(4), .enable("false")) decoder_1 (
    .out0(decoder_1_out0), .out1(decoder_1_out1), .out2(decoder_1_out2), .out3(decoder_1_out3),
    .out4(decoder_1_out4), .out5(decoder_1_out5), .out6(decoder_1_out6), .out7(decoder_1_out7),
    .out8(decoder_1_out8), .out9(decoder_1_out9), .out10(decoder_1_out10), .out11(decoder_1_out11),
    .out12(decoder_1_out12), .out13(decoder_1_out13), .out14(decoder_1_out14), .out15(decoder_1_out15),
    .sel(Read_register_2));
  and and_1 (and_1_out, Write, decoder_1_out0);
  and and_2 (and_2_out, Write, decoder_1_out1);
  and and_3 (and_3_out, Write, decoder_1_out2);
  and and_4 (and_4_out, Write, decoder_1_out3);
  and and_5 (and_5_out, Write, decoder_1_out4);
  and and_6 (and_6_out, Write, decoder_1_out5);
  and and_7 (and_7_out, Write, decoder_1_out6);
  and and_8 (and_8_out, Write, decoder_1_out7);
  and and_9 (and_9_out, Write, decoder_1_out8);
  and and_10 (and_10_out, Write, decoder_1_out9);
  and and_11 (and_11_out, Write, decoder_1_out10);
  and and_12 (and_12_out, Write, decoder_1_out11);
  and and_13 (and_13_out, Write, decoder_1_out12);
  and and_14 (and_14_out, Write, decoder_1_out13);
  and and_15 (and_15_out, Write, decoder_1_out14);
  and and_16 (and_16_out, Write, decoder_1_out15);
  Register #(.width(16)) register_1 (.D(in_1), .en(and_1_out), .Q(register_1_q), .clk(in_5));  // open: clr
  Register #(.width(16)) register_2 (.D(in_1), .en(and_2_out), .Q(register_2_q), .clk(in_5));  // open: clr
  Register #(.width(16)) register_3 (.D(in_1), .en(and_3_out), .Q(register_3_q), .clk(in_5));  // open: clr
  Register #(.width(16)) register_4 (.D(in_1), .en(and_4_out), .Q(register_4_q), .clk(in_5));  // open: clr
  Register #(.width(16)) register_5 (.D(in_1), .en(and_5_out), .Q(register_5_q), .clk(in_5));  // open: clr
  Register #(.width(16)) register_6 (.D(in_1), .en(and_6_out), .Q(register_6_q), .clk(in_5));  // open: clr
  Register #(.width(16)) register_7 (.D(in_1), .en(and_7_out), .Q(register_7_q), .clk(in_5));  // open: clr
  Register #(.width(16)) register_8 (.D(in_1), .en(and_8_out), .Q(register_8_q), .clk(in_5));  // open: clr
  Register #(.width(16)) register_9 (.D(in_1), .en(and_9_out), .Q(register_9_q), .clk(in_5));  // open: clr
  Register #(.width(16)) register_10 (.D(in_1), .en(and_10_out), .Q(register_10_q), .clk(in_5));  // open: clr
  Register #(.width(16)) register_11 (.D(in_1), .en(and_11_out), .Q(register_11_q), .clk(in_5));  // open: clr
  Register #(.width(16)) register_12 (.D(in_1), .en(and_12_out), .Q(register_12_q), .clk(in_5));  // open: clr
  Register #(.width(16)) register_13 (.D(in_1), .en(and_13_out), .Q(register_13_q), .clk(in_5));  // open: clr
  Register #(.width(16)) register_14 (.D(in_1), .en(and_14_out), .Q(register_14_q), .clk(in_5));  // open: clr
  Register #(.width(16)) register_15 (.D(in_1), .en(and_15_out), .Q(register_15_q), .clk(in_5));  // open: clr
  Register #(.width(16)) register_16 (.D(in_1), .en(and_16_out), .Q(register_16_q), .clk(in_5));  // open: clr
  Multiplexer #(.select(4), .width(16)) multiplexer_1 (
    .in0(register_1_q), .in1(register_2_q), .in2(register_3_q), .in3(register_4_q), .in4(register_5_q),
    .in5(register_6_q), .in6(register_7_q), .in7(register_8_q), .in8(register_9_q), .in9(register_10_q),
    .in10(register_11_q), .in11(register_12_q), .in12(register_13_q), .in13(register_14_q),
    .in14(register_15_q), .in15(register_16_q), .out(out_7), .sel(in_2));  // open: en
  Multiplexer #(.select(4), .width(16)) multiplexer_2 (
    .in0(register_1_q), .in1(register_2_q), .in2(register_3_q), .in3(register_4_q), .in4(register_5_q),
    .in5(register_6_q), .in6(register_7_q), .in7(register_8_q), .in8(register_9_q), .in9(register_10_q),
    .in10(register_11_q), .in11(register_12_q), .in12(register_13_q), .in13(register_14_q),
    .in14(register_15_q), .in15(register_16_q), .out(out_8), .sel(Register_number));  // open: en
  Multiplexer #(.select(4), .width(16), .enable("false")) multiplexer_3 (
    .in0(register_1_q), .in1(register_2_q), .in2(register_3_q), .in3(register_4_q), .in4(register_5_q),
    .in5(register_6_q), .in6(register_7_q), .in7(register_8_q), .in8(register_9_q), .in9(register_10_q),
    .in10(register_11_q), .in11(register_12_q), .in12(register_13_q), .in13(register_14_q),
    .in14(register_15_q), .in15(register_16_q), .out(out_9), .sel(Read_register_2));

  // Notes on the sheet:
  //   Read register 1
  //   Register data
  //   Clock
  //   Read data 1
  //   Read data 2
  //   Read data 3
endmodule

module Control (
  input  [3:0] in_1,
  output [3:0] _1,
  output _2,
  output _3,
  output _4,
  output _5,
  output _6,
  output _7,
  output _8,
  output [1:0] _1_2,
  output ldhi
);

  ROM #(.addrWidth(4), .dataWidth(13)) rom_1 (.addr(in_1), .data({_1_2, _8, _7, _6, _5, _4, _3, _2, _1}));  // open: sel
  ROM #(.addrWidth(4), .dataWidth(1)) rom_2 (.addr(in_1), .data(ldhi));  // open: sel

  // Notes on the sheet:
  //   contents of rom_1 (hex, n*v repeats v):
  //   112 113 52 182 111 110 114 0 332 272 1220 a20 0 630 0 1800
  //   contents of rom_2 (hex, n*v repeats v):
  //   9*0 1
  //   9
  //   2
  //   3
  //   4
  //   5
  //   6
  //   7
  //   8
  //   9
  //   ALU control
  //   Write Rd?
  //   ALU src
  //   memRead
  //   memWrite
  //   memReg
  //   RS 0 RD
  //   if jump
  //   PC src
endmodule

module ALU_adder (
  input  [15:0] in_1,
  input  [15:0] in_2,
  output [15:0] out_3
);

  Adder #(.width(16)) adder_1 (.a(in_1), .b(in_2), .out(out_3));  // open: cin, cout
endmodule

module _16_bit_ALU (
  input  [3:0] OP,
  input  [15:0] in_2,
  input  [15:0] in_3,
  output zero,
  output [15:0] out_5
);

  wire [15:0] adder_1_out, and_1_out, not_1_out, or_1_out, subtractor_1_out;

  assign or_1_out = in_2 | in_3;  // OR_Gate or_1, 16 bits wide
  assign and_1_out = in_2 & in_3;  // AND_Gate and_1, 16 bits wide
  Adder #(.width(16)) adder_1 (.a(in_2), .b(in_3), .out(adder_1_out));  // open: cin, cout
  Subtractor #(.width(16)) subtractor_1 (.a(in_2), .b(in_3), .out(subtractor_1_out));  // open: bin, bout
  assign not_1_out = ~in_2;  // NOT_Gate not_1, 16 bits wide
  Multiplexer #(.select(4), .width(16), .enable("false")) multiplexer_1 (
    .in0(or_1_out), .in1(and_1_out), .in2(adder_1_out), .in3(subtractor_1_out), .in4(not_1_out), .out(out_5),
    .sel(OP));  // open: in5, in6, in7, in8, in9, in10, in11, in12, in13, in14, in15
  Comparator #(.width(16)) comparator_1 (.a({16{1'b0}}), .b(in_2), .eq(zero));  // open: gt, lt

  // Notes on the sheet:
  //   a
  //   b
  //   RES
endmodule
